// Logisim project Programa_Principal.circ as structural Verilog: 10 circuits, main circuit ALU_1bit
module main (
  input  [15:0] ENTRADA,
  input  Clear_Cache,
  output [7:0] out_3,
  output out_4
);

  wire CLK, modulo_decoder_alu_1_cin, modulo_decoder_alu_1_s0, modulo_decoder_alu_1_s1,
       n7_segment_display_1_p1, n7_segment_display_2_p1, n7_segment_display_3_p1;
  wire [1:0] modulo_decoder_banco_1_code, modulo_decoder_banco_1_num_reg, modulo_decoder_banco_2_code,
       modulo_decoder_banco_2_num_reg, modulo_decoder_banco_3_code, modulo_decoder_banco_3_num_reg,
       modulo_decoder_banco_4_code, modulo_decoder_banco_4_num_reg, modulo_decoder_registro_1_codea,
       modulo_decoder_registro_1_codeb;
  wire [7:0] banco_4registros_1_out_6, banco_4registros_2_out_6, banco_4registros_3_out_6,
       banco_4registros_4_out_6, modulo_decoder_banco_1_reg_input, modulo_decoder_banco_2_reg_input,
       modulo_decoder_banco_3_reg_input, modulo_decoder_banco_4_reg_input,
       modulo_decoder_registro_1_reg_inputa, modulo_decoder_registro_1_reg_inputb, multiplexer_1_out,
       registro_despl_universal_8bits_1_q_8bits, registro_despl_universal_8bits_2_q_8bits;
  wire [15:0] demultiplexer_1_out0, demultiplexer_1_out1, demultiplexer_1_out2, demultiplexer_1_out3;

  Demultiplexer #(.select(2), .width(16)) demultiplexer_1 (
    .out0(demultiplexer_1_out0), .out1(demultiplexer_1_out1), .out2(demultiplexer_1_out2),
    .out3(demultiplexer_1_out3), .in(ENTRADA), .sel(ENTRADA[3:2]));
  Modulo_Decoder_Banco modulo_decoder_banco_1 (
    .In_16bits(demultiplexer_1_out0), .Reg_Input(modulo_decoder_banco_1_reg_input),
    .Code(modulo_decoder_banco_1_code), .Num_Reg(modulo_decoder_banco_1_num_reg));
  Modulo_Decoder_Banco modulo_decoder_banco_2 (
    .In_16bits(demultiplexer_1_out1), .Reg_Input(modulo_decoder_banco_2_reg_input),
    .Code(modulo_decoder_banco_2_code), .Num_Reg(modulo_decoder_banco_2_num_reg));
  Modulo_Decoder_Banco modulo_decoder_banco_3 (
    .In_16bits(demultiplexer_1_out2), .Reg_Input(modulo_decoder_banco_3_reg_input),
    .Code(modulo_decoder_banco_3_code), .Num_Reg(modulo_decoder_banco_3_num_reg));
  Modulo_Decoder_Banco modulo_decoder_banco_4 (
    .In_16bits(demultiplexer_1_out3), .Reg_Input(modulo_decoder_banco_4_reg_input),
    .Code(modulo_decoder_banco_4_code), .Num_Reg(modulo_decoder_banco_4_num_reg));
  // _7_Segment_Display 7_segment_display_1: pin names not known; wires that end beside it: n7_segment_display_1_p1, n7_segment_display_1_p1
  // _7_Segment_Display 7_segment_display_2: pin names not known; wires that end beside it: n7_segment_display_2_p1, n7_segment_display_2_p1
  // BCD_to_7_Segment_decoder bcd_to_7_segment_decoder_1: pin names not known
  // BCD_to_7_Segment_decoder bcd_to_7_segment_decoder_2: pin names not known
  // Binary_to_BCD_converter #(.binvalue(8)) binary_to_bcd_converter_1: pin names not known; wires that end beside it: ENTRADA[15:8]
  Clock clock_1 (.out(CLK));
  // _7_Segment_Display 7_segment_display_3: pin names not known; wires that end beside it: n7_segment_display_3_p1, n7_segment_display_3_p1
  // BCD_to_7_Segment_decoder bcd_to_7_segment_decoder_3: pin names not known
  Banco_4registros banco_4registros_1 (
    .CLK(CLK), .Reg_input(modulo_decoder_banco_1_reg_input), .Code(modulo_decoder_banco_1_code),
    .NumRegistro(modulo_decoder_banco_1_num_reg), .out_6(banco_4registros_1_out_6));  // open: Reset_Banco
  Banco_4registros banco_4registros_2 (
    .CLK(CLK), .Reg_input(modulo_decoder_banco_2_reg_input), .Code(modulo_decoder_banco_2_code),
    .NumRegistro(modulo_decoder_banco_2_num_reg), .out_6(banco_4registros_2_out_6));  // open: Reset_Banco
  Banco_4registros banco_4registros_3 (
    .CLK(CLK), .Reg_input(modulo_decoder_banco_3_reg_input), .Code(modulo_decoder_banco_3_code),
    .NumRegistro(modulo_decoder_banco_3_num_reg), .out_6(banco_4registros_3_out_6));  // open: Reset_Banco
  Banco_4registros banco_4registros_4 (
    .CLK(CLK), .Reg_input(modulo_decoder_banco_4_reg_input), .Code(modulo_decoder_banco_4_code),
    .NumRegistro(modulo_decoder_banco_4_num_reg), .out_6(banco_4registros_4_out_6));  // open: Reset_Banco
  Multiplexer #(.select(2), .width(8)) multiplexer_1 (
    .in0(banco_4registros_1_out_6), .in1(banco_4registros_2_out_6), .in2(banco_4registros_3_out_6),
    .in3(banco_4registros_4_out_6), .out(multiplexer_1_out), .sel(ENTRADA[3:2]));
  Modulo_Decoder_Registro modulo_decoder_registro_1 (
    .In_16bits(ENTRADA), .In_Memoria(multiplexer_1_out), .Reg_InputA(modulo_decoder_registro_1_reg_inputa),
    .CodeA(modulo_decoder_registro_1_codea), .Reg_InputB(modulo_decoder_registro_1_reg_inputb),
    .CodeB(modulo_decoder_registro_1_codeb));
  Modulo_Decoder_ALU modulo_decoder_alu_1 (
    .Entrada(ENTRADA), .S1(modulo_decoder_alu_1_s1), .S0(modulo_decoder_alu_1_s0),
    .Cin(modulo_decoder_alu_1_cin));
  Registro_despl_universal_8bits registro_despl_universal_8bits_1 (
    .D_8bits(modulo_decoder_registro_1_reg_inputa), .Code(modulo_decoder_registro_1_codea), .CLK(CLK),
    .CLEAR(Clear_Cache), .Q_8bits(registro_despl_universal_8bits_1_q_8bits));
  Registro_despl_universal_8bits registro_despl_universal_8bits_2 (
    .D_8bits(modulo_decoder_registro_1_reg_inputb), .Code(modulo_decoder_registro_1_codeb), .CLK(CLK),
    .CLEAR(Clear_Cache), .Q_8bits(registro_despl_universal_8bits_2_q_8bits));
  ALU_V2_8bit alu_v2_8bit_1 (
    .S1(modulo_decoder_alu_1_s1), .S0(modulo_decoder_alu_1_s0), .Cin(modulo_decoder_alu_1_cin),
    .A(registro_despl_universal_8bits_1_q_8bits), .B(registro_despl_universal_8bits_2_q_8bits), .F(out_3),
    .Cout(out_4));

  // Notes on the sheet:
  //   8bits numero | 2bits codigo de acción | 2bits número de registro | 2bits banco/caché a modificar | 2bit  operacion (ALU)
  //   01->Carga en registro 
  //   11->Opera con ALU
  //   00-> Carga en memoria un numero
  //   10->Carga resultado de ALU en memoria
endmodule

module ALU_1bit (
  input  Cin,
  input  [1:0] Code,
  input  A,
  input  B,
  output S,
  output Cout
);

  wire adder_1_cout, adder_1_out, and_1_out, or_1_out, subtractor_1_bout, subtractor_1_out;

  and and_1 (and_1_out, A, B);
  or or_1 (or_1_out, A, B);
  Adder #(.width(1)) adder_1 (.a(A), .b(B), .out(adder_1_out), .cin(Cin), .cout(adder_1_cout));
  Subtractor #(.width(1)) subtractor_1 (.a(A), .b(B), .out(subtractor_1_out), .bin(Cin), .bout(subtractor_1_bout));
  Multiplexer #(.select(2)) multiplexer_1 (
    .in0(and_1_out), .in1(or_1_out), .in2(adder_1_out), .in3(subtractor_1_out), .out(S), .sel(Code));
  Multiplexer #(.select(2)) multiplexer_2 (
    .in0(1'b0), .in1(1'b0), .in2(adder_1_cout), .in3(subtractor_1_bout), .out(Cout), .sel(Code));
endmodule

module ALU_8bits (
  input  [7:0] A,
  input  [7:0] B,
  input  [1:0] Code,
  input  Cin,
  output [7:0] S,
  output Cout
);

  wire alu_1bit_1_cout, alu_1bit_2_cout, alu_1bit_3_cout, alu_1bit_4_cout, alu_1bit_5_cout, alu_1bit_6_cout,
       alu_1bit_7_cout;

  ALU_1bit alu_1bit_1 (.Cin(Cin), .Code(Code), .A(A[0]), .B(B[0]), .S(S[0]), .Cout(alu_1bit_1_cout));
  ALU_1bit alu_1bit_2 (.Cin(alu_1bit_1_cout), .Code(Code), .A(A[1]), .B(B[1]), .S(S[1]), .Cout(alu_1bit_2_cout));
  ALU_1bit alu_1bit_3 (.Cin(alu_1bit_2_cout), .Code(Code), .A(A[2]), .B(B[2]), .S(S[2]), .Cout(alu_1bit_3_cout));
  ALU_1bit alu_1bit_4 (.Cin(alu_1bit_3_cout), .Code(Code), .A(A[3]), .B(B[3]), .S(S[3]), .Cout(alu_1bit_4_cout));
  ALU_1bit alu_1bit_5 (.Cin(alu_1bit_4_cout), .Code(Code), .A(A[4]), .B(B[4]), .S(S[4]), .Cout(alu_1bit_5_cout));
  ALU_1bit alu_1bit_6 (.Cin(alu_1bit_5_cout), .Code(Code), .A(A[5]), .B(B[5]), .S(S[5]), .Cout(alu_1bit_6_cout));
  ALU_1bit alu_1bit_7 (.Cin(alu_1bit_6_cout), .Code(Code), .A(A[6]), .B(B[6]), .S(S[6]), .Cout(alu_1bit_7_cout));
  ALU_1bit alu_1bit_8 (.Cin(alu_1bit_7_cout), .Code(Code), .A(A[7]), .B(B[7]), .S(S[7]), .Cout(Cout));
endmodule

module Registro_8bits (
  input  [7:0] in_1,
  input  in_2,
  input  [7:0] D_in,
  input  CLK,
  input  CLEAR,
  output [7:0] out_6,
  output [7:0] Q_out
);

  Register register_1 (.D(in_1), .en(1'b1), .clk(in_2), .Q(out_6));  // open: clr
  D_Flip_Flop d_ff_1 (.D(D_in[7]), .clk(CLK), .Q(Q_out[7]), .reset(CLEAR));  // open: Qn, preset
  D_Flip_Flop d_ff_2 (.D(D_in[6]), .clk(CLK), .Q(Q_out[6]), .reset(CLEAR));  // open: Qn, preset
  D_Flip_Flop d_ff_3 (.D(D_in[5]), .clk(CLK), .Q(Q_out[5]), .reset(CLEAR));  // open: Qn, preset
  D_Flip_Flop d_ff_4 (.D(D_in[4]), .clk(CLK), .Q(Q_out[4]), .reset(CLEAR));  // open: Qn, preset
  D_Flip_Flop d_ff_5 (.D(D_in[3]), .clk(CLK), .Q(Q_out[3]), .reset(CLEAR));  // open: Qn, preset
  D_Flip_Flop d_ff_6 (.D(D_in[2]), .clk(CLK), .Q(Q_out[2]), .reset(CLEAR));  // open: Qn, preset
  D_Flip_Flop d_ff_7 (.D(D_in[1]), .clk(CLK), .Q(Q_out[1]), .reset(CLEAR));  // open: Qn, preset
  D_Flip_Flop d_ff_8 (.D(D_in[0]), .clk(CLK), .Q(Q_out[0]), .reset(CLEAR));  // open: Qn, preset
endmodule

module Registro_despl_universal_8bits (
  input  [7:0] D_8bits,
  input  [1:0] Code,
  input  CLK,
  input  CLEAR,
  output [7:0] Q_8bits
);

  wire multiplexer_1_out, multiplexer_2_out, multiplexer_3_out, multiplexer_4_out, multiplexer_5_out,
       multiplexer_6_out, multiplexer_7_out, multiplexer_8_out;

  Multiplexer #(.select(2)) multiplexer_1 (
    .in0(Q_8bits[7]), .in1(1'b0), .in2(Q_8bits[6]), .in3(D_8bits[7]), .out(multiplexer_1_out), .sel(Code));
  D_Flip_Flop d_ff_1 (.D(multiplexer_1_out), .clk(CLK), .Q(Q_8bits[7]), .reset(CLEAR));  // open: Qn, preset
  Multiplexer #(.select(2)) multiplexer_2 (
    .in0(Q_8bits[6]), .in1(Q_8bits[7]), .in2(Q_8bits[5]), .in3(D_8bits[6]), .out(multiplexer_2_out),
    .sel(Code));
  D_Flip_Flop d_ff_2 (.D(multiplexer_2_out), .clk(CLK), .Q(Q_8bits[6]), .reset(CLEAR));  // open: Qn, preset
  Multiplexer #(.select(2)) multiplexer_3 (
    .in0(Q_8bits[5]), .in1(Q_8bits[6]), .in2(Q_8bits[4]), .in3(D_8bits[5]), .out(multiplexer_3_out),
    .sel(Code));
  D_Flip_Flop d_ff_3 (.D(multiplexer_3_out), .clk(CLK), .Q(Q_8bits[5]), .reset(CLEAR));  // open: Qn, preset
  Multiplexer #(.select(2)) multiplexer_4 (
    .in0(Q_8bits[4]), .in1(Q_8bits[5]), .in2(Q_8bits[3]), .in3(D_8bits[4]), .out(multiplexer_4_out),
    .sel(Code));
  D_Flip_Flop d_ff_4 (.D(multiplexer_4_out), .clk(CLK), .Q(Q_8bits[4]), .reset(CLEAR));  // open: Qn, preset
  Multiplexer #(.select(2)) multiplexer_5 (
    .in0(Q_8bits[3]), .in1(Q_8bits[4]), .in2(Q_8bits[2]), .in3(D_8bits[3]), .out(multiplexer_5_out),
    .sel(Code));
  D_Flip_Flop d_ff_5 (.D(multiplexer_5_out), .clk(CLK), .Q(Q_8bits[3]), .reset(CLEAR));  // open: Qn, preset
  Multiplexer #(.select(2)) multiplexer_6 (
    .in0(Q_8bits[2]), .in1(Q_8bits[3]), .in2(Q_8bits[1]), .in3(D_8bits[2]), .out(multiplexer_6_out),
    .sel(Code));
  D_Flip_Flop d_ff_6 (.D(multiplexer_6_out), .clk(CLK), .Q(Q_8bits[2]), .reset(CLEAR));  // open: Qn, preset
  Multiplexer #(.select(2)) multiplexer_7 (
    .in0(Q_8bits[1]), .in1(Q_8bits[2]), .in2(Q_8bits[0]), .in3(D_8bits[1]), .out(multiplexer_7_out),
    .sel(Code));
  D_Flip_Flop d_ff_7 (.D(multiplexer_7_out), .clk(CLK), .Q(Q_8bits[1]), .reset(CLEAR));  // open: Qn, preset
  Multiplexer #(.select(2)) multiplexer_8 (
    .in0(Q_8bits[0]), .in1(Q_8bits[1]), .in2(1'b0), .in3(D_8bits[0]), .out(multiplexer_8_out), .sel(Code));
  D_Flip_Flop d_ff_8 (.D(multiplexer_8_out), .clk(CLK), .Q(Q_8bits[0]), .reset(CLEAR));  // open: Qn, preset

  // Notes on the sheet:
  //   00 keep 01 shift right 10 shift left 11 load
endmodule

module Banco_4registros (
  input  CLK,
  input  Reset_Banco,
  input  [7:0] Reg_input,
  input  [1:0] Code,
  input  [1:0] NumRegistro,
  output [7:0] out_6
);

  wire [7:0] registro_despl_universal_8bits_1_q_8bits, registro_despl_universal_8bits_2_q_8bits,
       registro_despl_universal_8bits_3_q_8bits, registro_despl_universal_8bits_4_q_8bits;
  wire [9:0] demultiplexer_1_out0, demultiplexer_1_out1, demultiplexer_1_out2, demultiplexer_1_out3;

  Demultiplexer #(.select(2), .width(10)) demultiplexer_1 (
    .out0(demultiplexer_1_out0), .out1(demultiplexer_1_out1), .out2(demultiplexer_1_out2),
    .out3(demultiplexer_1_out3), .in({Code, Reg_input}), .sel(NumRegistro));
  Registro_despl_universal_8bits registro_despl_universal_8bits_1 (
    .D_8bits(demultiplexer_1_out0[7:0]), .Code(demultiplexer_1_out0[9:8]), .CLK(CLK), .CLEAR(Reset_Banco),
    .Q_8bits(registro_despl_universal_8bits_1_q_8bits));
  Registro_despl_universal_8bits registro_despl_universal_8bits_2 (
    .D_8bits(demultiplexer_1_out1[7:0]), .Code(demultiplexer_1_out1[9:8]), .CLK(CLK), .CLEAR(Reset_Banco),
    .Q_8bits(registro_despl_universal_8bits_2_q_8bits));
  Registro_despl_universal_8bits registro_despl_universal_8bits_3 (
    .D_8bits(demultiplexer_1_out2[7:0]), .Code(demultiplexer_1_out2[9:8]), .CLK(CLK), .CLEAR(Reset_Banco),
    .Q_8bits(registro_despl_universal_8bits_3_q_8bits));
  Registro_despl_universal_8bits registro_despl_universal_8bits_4 (
    .D_8bits(demultiplexer_1_out3[7:0]), .Code(demultiplexer_1_out3[9:8]), .CLK(CLK), .CLEAR(Reset_Banco),
    .Q_8bits(registro_despl_universal_8bits_4_q_8bits));
  Multiplexer #(.select(2), .width(8)) multiplexer_1 (
    .in0(registro_despl_universal_8bits_1_q_8bits), .in1(registro_despl_universal_8bits_2_q_8bits),
    .in2(registro_despl_universal_8bits_3_q_8bits), .in3(registro_despl_universal_8bits_4_q_8bits),
    .out(out_6), .sel(NumRegistro));
endmodule

module Modulo_Decoder_Banco (
  input  [15:0] In_16bits,
  output [7:0] Reg_Input,
  output [1:0] Code,
  output [1:0] Num_Reg
);

  Multiplexer #(.select(2), .width(12)) multiplexer_1 (
    .in0(In_16bits[15:4]), .in1({{10{1'b0}}, In_16bits[5:4]}), .in2({12{1'b0}}), .in3({12{1'b0}}),
    .out({Reg_Input, Code, Num_Reg}), .sel(In_16bits[1:0]));

  // Notes on the sheet:
  //   Numero
  //   8bits numero | 2bits codigo de acción | 2bits número de registro | 2bits banco/caché a modificar | 1bit  operacion (ALU)
endmodule

module Modulo_Decoder_Registro (
  input  [15:0] In_16bits,
  input  [7:0] In_Memoria,
  output [7:0] Reg_InputA,
  output [1:0] CodeA,
  output [7:0] Reg_InputB,
  output [1:0] CodeB
);

  wire multiplexer_3_out;
  wire [1:0] multiplexer_4_out;
  wire [7:0] multiplexer_2_out;
  wire [15:0] demultiplexer_1_out0, multiplexer_1_out;

  Multiplexer #(.select(2), .width(16)) multiplexer_1 (
    .in0({16{1'b0}}), .in1(In_16bits), .in2({16{1'b0}}), .in3({16{1'b0}}), .out(multiplexer_1_out),
    .sel(In_16bits[1:0]));
  Demultiplexer #(.width(16)) demultiplexer_1 (
    .out0(demultiplexer_1_out0), .in(multiplexer_1_out), .sel(In_16bits[7]));  // open: out1
  Multiplexer #(.width(8)) multiplexer_2 (
    .in0(demultiplexer_1_out0[15:8]), .in1(In_Memoria), .out(multiplexer_2_out), .sel(In_16bits[7]));
  Multiplexer multiplexer_3 (
    .in0(demultiplexer_1_out0[2]), .in1(In_16bits[6]), .out(multiplexer_3_out), .sel(In_16bits[7]));
  Multiplexer #(.width(2)) multiplexer_4 (
    .in0(demultiplexer_1_out0[4:3]), .in1({2{In_16bits[7]}}), .out(multiplexer_4_out), .sel(In_16bits[7]));
  Demultiplexer #(.width(8)) demultiplexer_2 (
    .out0(Reg_InputA), .out1(Reg_InputB), .in(multiplexer_2_out), .sel(multiplexer_3_out));
  Demultiplexer #(.width(2)) demultiplexer_3 (
    .out0(CodeA), .out1(CodeB), .in(multiplexer_4_out), .sel(multiplexer_3_out));

  // Other names for the same wires on the sheet: Option01 = In_16bits[7]

  // Notes on the sheet:
  //   Numero
endmodule

module ALU_V2_8bit (
  input  S1,
  input  S0,
  input  Cin,
  input  [7:0] A,
  input  [7:0] B,
  output [7:0] F,
  output Cout
);

  wire adder_1_cout, adder_2_cout, adder_3_cout, adder_4_cout, adder_5_cout, adder_6_cout, adder_7_cout,
       and_1_out, and_2_out, and_3_out, and_4_out, and_5_out, and_6_out, and_7_out, and_8_out, and_9_out,
       and_10_out, and_11_out, and_12_out, and_13_out, and_14_out, and_15_out, and_16_out, not_1_out,
       not_2_out, not_3_out, not_4_out, not_5_out, not_6_out, not_7_out, not_8_out, or_1_out, or_2_out,
       or_3_out, or_4_out, or_5_out, or_6_out, or_7_out, or_8_out;

  not not_1 (not_1_out, B[0]);
  not not_2 (not_2_out, B[1]);
  not not_3 (not_3_out, B[2]);
  not not_4 (not_4_out, B[3]);
  not not_5 (not_5_out, B[4]);
  not not_6 (not_6_out, B[5]);
  not not_7 (not_7_out, B[6]);
  not not_8 (not_8_out, B[7]);
  and and_1 (and_1_out, B[0], S0);
  and and_2 (and_2_out, not_1_out, S1);
  and and_3 (and_3_out, B[1], S0);
  and and_4 (and_4_out, not_2_out, S1);
  and and_5 (and_5_out, B[2], S0);
  and and_6 (and_6_out, not_3_out, S1);
  and and_7 (and_7_out, B[3], S0);
  and and_8 (and_8_out, not_4_out, S1);
  and and_9 (and_9_out, B[4], S0);
  and and_10 (and_10_out, not_5_out, S1);
  and and_11 (and_11_out, B[5], S0);
  and and_12 (and_12_out, not_6_out, S1);
  and and_13 (and_13_out, B[6], S0);
  and and_14 (and_14_out, not_7_out, S1);
  and and_15 (and_15_out, B[7], S0);
  and and_16 (and_16_out, not_8_out, S1);
  Adder #(.width(1)) adder_1 (.a(A[0]), .b(or_1_out), .out(F[0]), .cin(Cin), .cout(adder_1_cout));
  or or_1 (or_1_out, and_1_out, and_2_out);
  Adder #(.width(1)) adder_2 (.a(A[1]), .b(or_2_out), .out(F[1]), .cin(adder_1_cout), .cout(adder_2_cout));
  or or_2 (or_2_out, and_3_out, and_4_out);
  Adder #(.width(1)) adder_3 (.a(A[2]), .b(or_3_out), .out(F[2]), .cin(adder_2_cout), .cout(adder_3_cout));
  or or_3 (or_3_out, and_5_out, and_6_out);
  Adder #(.width(1)) adder_4 (.a(A[3]), .b(or_4_out), .out(F[3]), .cin(adder_3_cout), .cout(adder_4_cout));
  or or_4 (or_4_out, and_7_out, and_8_out);
  Adder #(.width(1)) adder_5 (.a(A[4]), .b(or_5_out), .out(F[4]), .cin(adder_4_cout), .cout(adder_5_cout));
  or or_5 (or_5_out, and_9_out, and_10_out);
  Adder #(.width(1)) adder_6 (.a(A[5]), .b(or_6_out), .out(F[5]), .cin(adder_5_cout), .cout(adder_6_cout));
  or or_6 (or_6_out, and_11_out, and_12_out);
  Adder #(.width(1)) adder_7 (.a(A[6]), .b(or_7_out), .out(F[6]), .cin(adder_6_cout), .cout(adder_7_cout));
  or or_7 (or_7_out, and_13_out, and_14_out);
  Adder #(.width(1)) adder_8 (.a(A[7]), .b(or_8_out), .out(F[7]), .cin(adder_7_cout), .cout(Cout));
  or or_8 (or_8_out, and_15_out, and_16_out);
endmodule

module Modulo_Decoder_ALU (
  input  [15:0] Entrada,
  output S1,
  output S0,
  output Cin
);

  Multiplexer #(.select(2), .width(3)) multiplexer_1 (
    .in0(3'b000), .in1(3'b000), .in2(3'b000), .in3(Entrada[4:2]), .out({S1, S0, Cin}), .sel(Entrada[1:0]));
endmodule
